# Fritzing sketch blink (saved by Fritzing 0.9.3b)
breadboards: 1

parts:
  Componente1 = Arduino Uno (Rev3) - ICSP  # not connected
  LED2 = smd LED [color="Blue (430nm)" package="0603 [SMD]"]
  R1 = Resistor [tolerance=±5% resistance=150 package="2010 [SMD]"]

nets:
  N1: LED2.anode, R1.Pin_1
