# Fritzing sketch btn (saved by Fritzing 0.9.3b)
breadboards: 1

parts:
  Componente1 = Arduino Uno (Rev3) - ICSP
  S1 = Pushbutton [package="[THT]"]
  R1 = Resistor [tolerance=±5% resistance=220 package="0805 [SMD]"]

nets:
  N1: Componente1.D2, S1.Pin_3, S1.Pin_4, R1.Pin_1
  N2: Componente1.GND, R1.Pin_0
  N3: Componente1.VIN, S1.Pin_1, S1.Pin_2
